# Fritzing sketch scheme (saved by Fritzing 0.9.3b)

parts:
  U1 = LIPO-1000mAh [package=lipo-1000]
  U2 = LIPO-1000mAh [package=lipo-1000]
  U3 = LIPO-1000mAh [package=lipo-1000]
  U4 = ESP8266 WiFi Module [part_number=ESP8266]
  Часть1 = InvenSense MPU6050
  J4 = Basic Servo
  J5 = Basic Servo
  J7 = Basic Servo  # not connected
  J8 = female pin header, 3 pins [form="♀ (female)"]  # not connected
  J9 = female pin header, 3 pins [form="♀ (female)"]  # not connected
  J10 = female pin header, 3 pins [form="♀ (female)"]
  J11 = female pin header, 3 pins [form="♀ (female)"]
  J6 = Basic Servo  # not connected
  Часть3 = Arduino Pro Mini v13
  U5 = DC-DC_CONVERTER [package=dc-dc_converter]
  J14 = female pin header, 2 pins [form="♀ (female)"]
  J15 = female pin header, 2 pins [form="♀ (female)"]
  R1 = Resistor [tolerance=±5% resistance=1k package=THT]
  R2 = Resistor [tolerance=±5% resistance=1k package=THT]
  J3 = female pin header, 4 pins [form="♀ (female)"]
  J16 = female pin header, 4 pins [form="♀ (female)"]
  J17 = female pin header, 4 pins [form="♀ (female)"]
  J18 = female pin header, 4 pins [form="♀ (female)"]

nets:
  N1: U1.+, J15.pin1
  N2: U1.-, U2.+
  N3: U2.-, U3.+
  N4: U3.-, J15.pin2
  N5: U4.RXD, Часть3.D7
  N6: U4.VCC, U5.ON_OFF, R1.Pin_1
  N7: U4.GND, U5.VOUT, R2.Pin_0
  N8: U4.TXD, Часть3.D8
  N9: U4.GPIO_15, R2.Pin_1
  N10: U4.ADC_0, R1.Pin_0
  VCC: Часть1.VCC, Часть3.VCC
  N11: Часть1.SCL, Часть3.A5
  N12: Часть1.SDA, Часть3.A4
  N13: J4.gnd, J11.pin1
  N14: J4.vcc, J11.pin2
  N15: J4.pulse, J11.pin3
  N16: J5.gnd, J10.pin1
  N17: J5.vcc, J10.pin2
  N18: J5.pulse, J10.pin3
  N19: Часть3.RAW, U5.VIN
  N20: Часть3.GND, U5.SENSE
  N21: Часть3.D9_PWM, J3.pin2
  N22: Часть3.D6_PWM, J18.pin2
  N23: Часть3.D5_PWM, J16.pin2
  N24: Часть3.D3_PWM, J17.pin2
  N25: U5.SEQ, J14.pin2

notes:
  2S 1P LiPo
  4x (1104 7500KV)
  MPU-6050
  SCL ->A5
  SDA -> A4
  7.4V -> 3.3V
  ESP-12
